# Fritzing sketch Circuit (saved by Fritzing 0.9.4)
breadboards: 1

parts:
  WeMos_D1_Mini1 = WeMos D1 Mini
  Part1 = Arduino Nano (Rev3.0)
  U1 = 4-Channel 5v Relay Shield [package=relay-4ch5v10a]
  U2 = LIPO-1000mAh [package=lipo-1000]
  Part2 = DHT22 module
  S1 = Square Pushbutton

nets:
  VCC: WeMos_D1_Mini1.5V, Part1.VIN, U1.VCC, U2.+, Part2.VCC
  N1: WeMos_D1_Mini1.D7, S1.leg0
  GND: WeMos_D1_Mini1.G, Part1.GND, U1.GND, U2.-, Part2.GND
  N2: WeMos_D1_Mini1.RX, Part1.D1/TX
  N3: WeMos_D1_Mini1.TX, Part1.D0/RX
  N4: Part1.D4, Part2.DATA
  N5: Part1.D5, U1.IN4
  N6: Part1.D6, U1.IN3
  N7: Part1.D7, S1.leg1
  N8: Part1.D8, U1.IN2
  N9: Part1.D9, U1.IN1

custom parts:
  4-Channel 5v Relay Shield: 4 Channel 5v Relay Shield w. 2x SPD-06VDC-SD-C
